// Logisim project 4BitCPU.circ as structural Verilog: 1 circuit, main circuit main
module main (
  input  [15:0] INSTRUCTION,
  input  in_2,
  input  in_3,
  input  [7:0] literally_just_4,
  output [15:0] hi
);

  wire and_1_out, and_2_out, and_3_out, and_4_out, and_5_out, and_6_out, and_7_out, and_8_out, clock_1_out,
       not_1_out, not_2_out, not_3_out, not_4_out;
  wire [3:0] adder_2_out, divider_1_out, multiplexer_1_out, multiplexer_2_out, multiplexer_3_out,
       multiplier_1_out, r0_q, r1_q, r2_q, r3_q, subtractor_1_out;
  wire [7:0] adder_1_out, PC_q;

  Clock clock_1 (.out(clock_1_out));
  not not_1 (not_1_out, INSTRUCTION[2]);
  and and_1 (and_1_out, not_1_out, not_2_out);
  not not_2 (not_2_out, INSTRUCTION[3]);
  and and_2 (and_2_out, INSTRUCTION[2], not_3_out);
  not not_3 (not_3_out, INSTRUCTION[3]);
  not not_4 (not_4_out, INSTRUCTION[2]);
  and and_3 (and_3_out, not_4_out, INSTRUCTION[3]);
  and and_4 (and_4_out, INSTRUCTION[2], INSTRUCTION[3]);
  Register #(.width(4)) r0 (.D(multiplexer_3_out), .en(and_5_out), .clk(clock_1_out), .Q(r0_q));  // open: clr
  and and_5 (and_5_out, INSTRUCTION[15], and_1_out);
  Register #(.width(4)) r1 (.D(multiplexer_3_out), .en(and_6_out), .clk(clock_1_out), .Q(r1_q));  // open: clr
  and and_6 (and_6_out, INSTRUCTION[15], and_2_out);
  Register #(.width(4)) r2 (.D(multiplexer_3_out), .en(and_7_out), .clk(clock_1_out), .Q(r2_q));  // open: clr
  and and_7 (and_7_out, INSTRUCTION[15], and_3_out);
  Register #(.width(4)) r3 (.D(multiplexer_3_out), .en(and_8_out), .clk(clock_1_out), .Q(r3_q));  // open: clr
  and and_8 (and_8_out, INSTRUCTION[15], and_4_out);
  Register PC (.D(adder_1_out), .en(clock_1_out), .clk(clock_1_out), .Q(PC_q));  // open: clr
  Adder adder_1 (.a(PC_q), .b(literally_just_4), .out(adder_1_out));  // open: cin, cout
  Multiplexer #(.select(2), .width(4)) multiplexer_1 (
    .in0(r0_q), .in1(r1_q), .in2(r2_q), .in3(r3_q), .out(multiplexer_1_out), .sel(INSTRUCTION[1:0]));
  Multiplexer #(.select(2), .width(4)) multiplexer_2 (
    .in0(r0_q), .in1(r1_q), .in2(r2_q), .in3(r3_q), .out(multiplexer_2_out), .sel(INSTRUCTION[3:2]));
  Multiplexer #(.select(2), .width(4)) multiplexer_3 (
    .in0(adder_2_out), .in1(subtractor_1_out), .in2(multiplier_1_out), .in3(divider_1_out),
    .out(multiplexer_3_out), .sel(INSTRUCTION[9:8]));
  RAM #(.asyncread("true"), .dataWidth(16)) progmem (
    .addr(PC_q), .we(in_2), .oe(in_3), .clk(clock_1_out), .dout(hi));  // open: din
  Adder #(.width(4)) adder_2 (.a(multiplexer_1_out), .b(multiplexer_2_out), .out(adder_2_out));  // open: cin, cout
  Subtractor #(.width(4)) subtractor_1 (
    .a(multiplexer_2_out), .b(multiplexer_1_out), .out(subtractor_1_out));  // open: bin, bout
  Multiplier #(.width(4)) multiplier_1 (
    .a(multiplexer_1_out), .b(multiplexer_2_out), .out(multiplier_1_out));  // open: cin, cout
  Divider #(.width(4)) divider_1 (
    .a(multiplexer_2_out), .b(multiplexer_1_out), .out(divider_1_out));  // open: upper, rem
endmodule
